// Logisim project 1-2,3,4.circ as structural Verilog: 1 circuit, main circuit main
module main (
  input  A,
  input  in_2,
  output And,
  output Or,
  output Not
);

  not not_1 (Not, A);
  and and_1 (And, A, in_2);
  or or_1 (Or, A, in_2);

  // Notes on the sheet:
  //   B
endmodule
