// Logisim project 1-5.circ as structural Verilog: 1 circuit, main circuit main
module main (
  input  A,
  input  Ena,
  output Tri
);

  assign Tri = Ena ? A : 1'bz;  // Controlled_Buffer controlled_buffer_1
endmodule
