// Logisim project selector14.circ as structural Verilog: 1 circuit, main circuit main
module main (
  input  S1,
  input  S2,
  input  D,
  output F0,
  output F1,
  output F2,
  output F3
);

  or or_1 (F0, S1, D, S2);
  or or_2 (F1, S1, D, ~S2);  // OR_Gate
  or or_3 (F2, ~S1, D, S2);  // OR_Gate
  or or_4 (F3, ~S1, D, ~S2);  // OR_Gate
endmodule
