// Logisim project selector14_4bits.circ as structural Verilog: 1 circuit, main circuit main
module main (
  input  S0,
  input  S1,
  input  [3:0] C,
  output [3:0] F0,
  output [3:0] F1,
  output [3:0] F2,
  output [3:0] F3
);

  wire [3:0] bit_extender_1_out, bit_extender_2_out;

  assign bit_extender_1_out = {{3{S0}}, S0};  // Bit_Extender bit_extender_1
  assign bit_extender_2_out = {{3{S1}}, S1};  // Bit_Extender bit_extender_2
  assign F0 = bit_extender_1_out | C | bit_extender_2_out;  // OR_Gate or_1, 4 bits wide
  assign F1 = ~bit_extender_1_out | C | bit_extender_2_out;  // OR_Gate or_2, 4 bits wide
  assign F2 = bit_extender_1_out | C | ~bit_extender_2_out;  // OR_Gate or_3, 4 bits wide
  assign F3 = ~bit_extender_1_out | C | ~bit_extender_2_out;  // OR_Gate or_4, 4 bits wide
endmodule
