// Logisim project selector41.circ as structural Verilog: 1 circuit, main circuit main
module main (
  input  S0,
  input  S1,
  input  C0,
  input  C1,
  input  C2,
  input  C3,
  output Z
);

  wire and_1_out, and_2_out, and_3_out, and_4_out;

  and and_1 (and_1_out, ~S0, C0, ~S1);  // AND_Gate
  and and_2 (and_2_out, S0, C1, ~S1);  // AND_Gate
  and and_3 (and_3_out, ~S0, C2, S1);  // AND_Gate
  and and_4 (and_4_out, S0, C3, S1);
  or or_1 (Z, and_1_out, and_2_out, and_3_out, and_4_out);
endmodule
