// Logisim project selector41_4bits.circ as structural Verilog: 1 circuit, main circuit main
module main (
  input  S0,
  input  S1,
  input  [3:0] C0,
  input  [3:0] C1,
  input  [3:0] C2,
  input  [3:0] C3,
  output [3:0] Z
);

  wire [3:0] and_1_out, and_2_out, and_3_out, and_4_out, bit_extender_1_out, bit_extender_2_out;

  assign bit_extender_1_out = {{3{S0}}, S0};  // Bit_Extender bit_extender_1
  assign bit_extender_2_out = {{3{S1}}, S1};  // Bit_Extender bit_extender_2
  assign and_1_out = ~bit_extender_1_out & C0 & ~bit_extender_2_out;  // AND_Gate and_1, 4 bits wide
  assign and_2_out = bit_extender_1_out & C1 & ~bit_extender_2_out;  // AND_Gate and_2, 4 bits wide
  assign and_3_out = ~bit_extender_1_out & C2 & bit_extender_2_out;  // AND_Gate and_3, 4 bits wide
  assign and_4_out = bit_extender_1_out & C3 & bit_extender_2_out;  // AND_Gate and_4, 4 bits wide
  assign Z = and_1_out | and_2_out | and_3_out | and_4_out;  // OR_Gate or_1, 4 bits wide
endmodule
