// Logisim project transmission8.circ as structural Verilog: 1 circuit, main circuit main
module main (
  input  S2,
  input  S1,
  input  S0,
  input  [7:0] D0,
  input  [7:0] D1,
  input  [7:0] D2,
  input  [7:0] D3,
  input  [7:0] D4,
  input  [7:0] D5,
  input  [7:0] D6,
  input  [7:0] D7,
  output [7:0] F0,
  output [7:0] F1,
  output [7:0] F2,
  output [7:0] F3,
  output [7:0] F4,
  output [7:0] F5,
  output [7:0] F6,
  output [7:0] F7
);

  wire [7:0] and_1_out, and_2_out, and_3_out, and_4_out, and_5_out, and_6_out, and_7_out, and_8_out,
       bit_extender_1_out, bit_extender_2_out, bit_extender_3_out, or_1_out;

  assign bit_extender_1_out = {{7{S2}}, S2};  // Bit_Extender bit_extender_1
  assign bit_extender_2_out = {{7{S1}}, S1};  // Bit_Extender bit_extender_2
  assign and_1_out = ~bit_extender_1_out & ~bit_extender_2_out & D0 & ~bit_extender_3_out;  // AND_Gate and_1, 8 bits wide
  assign and_2_out = ~bit_extender_1_out & ~bit_extender_2_out & D1 & bit_extender_3_out;  // AND_Gate and_2, 8 bits wide
  assign and_3_out = ~bit_extender_1_out & bit_extender_2_out & D2 & ~bit_extender_3_out;  // AND_Gate and_3, 8 bits wide
  assign and_4_out = ~bit_extender_1_out & bit_extender_2_out & D3 & bit_extender_3_out;  // AND_Gate and_4, 8 bits wide
  assign and_5_out = bit_extender_1_out & ~bit_extender_2_out & D4 & ~bit_extender_3_out;  // AND_Gate and_5, 8 bits wide
  assign and_6_out = bit_extender_1_out & ~bit_extender_2_out & D5 & bit_extender_3_out;  // AND_Gate and_6, 8 bits wide
  assign and_7_out = bit_extender_1_out & bit_extender_2_out & D6 & ~bit_extender_3_out;  // AND_Gate and_7, 8 bits wide
  assign and_8_out = bit_extender_1_out & bit_extender_2_out & D7 & bit_extender_3_out;  // AND_Gate and_8, 8 bits wide
  assign or_1_out = and_1_out | and_2_out | and_3_out | and_4_out | and_5_out | and_6_out | and_7_out | and_8_out;  // OR_Gate or_1, 8 bits wide
  assign bit_extender_3_out = {{7{S0}}, S0};  // Bit_Extender bit_extender_3
  assign F0 = bit_extender_1_out | bit_extender_2_out | or_1_out | bit_extender_3_out;  // OR_Gate or_2, 8 bits wide
  assign F1 = bit_extender_1_out | bit_extender_2_out | or_1_out | ~bit_extender_3_out;  // OR_Gate or_3, 8 bits wide
  assign F2 = bit_extender_1_out | ~bit_extender_2_out | or_1_out | bit_extender_3_out;  // OR_Gate or_4, 8 bits wide
  assign F3 = bit_extender_1_out | ~bit_extender_2_out | or_1_out | ~bit_extender_3_out;  // OR_Gate or_5, 8 bits wide
  assign F4 = ~bit_extender_1_out | bit_extender_2_out | or_1_out | bit_extender_3_out;  // OR_Gate or_6, 8 bits wide
  assign F5 = ~bit_extender_1_out | bit_extender_2_out | or_1_out | ~bit_extender_3_out;  // OR_Gate or_7, 8 bits wide
  assign F6 = ~bit_extender_1_out | ~bit_extender_2_out | or_1_out | bit_extender_3_out;  // OR_Gate or_8, 8 bits wide
  assign F7 = ~bit_extender_1_out | ~bit_extender_2_out | or_1_out | ~bit_extender_3_out;  // OR_Gate or_9, 8 bits wide
endmodule
