// Logisim project barrelshifter32.circ as structural Verilog: 2 circuits, main circuit MUX21
module MUX21 (
  input  S1,
  input  S2,
  input  C,
  input  Ena,
  output D
);

  wire and_1_out, and_2_out;

  and and_1 (and_1_out, S1, ~C, Ena);  // AND_Gate
  and and_2 (and_2_out, S2, C, Ena);
  or or_1 (D, and_1_out, and_2_out);
endmodule

// MUXLayer
module Layer (
  input  [7:0] in_1,
  input  aluc1,
  input  aluc0,
  input  Ena,
  input  [2:0] in_5,
  output [7:0] out_6
);

  wire and_1_out, mux21_1_d, mux21_2_d, mux21_3_d, mux21_4_d, mux21_5_d, mux21_6_d, mux21_7_d, mux21_8_d,
       mux21_9_d, mux21_10_d, mux21_11_d, mux21_12_d, mux21_13_d, mux21_14_d, mux21_15_d, mux21_16_d,
       mux21_17_d, mux21_18_d, mux21_19_d, mux21_20_d, mux21_21_d, mux21_22_d, mux21_23_d, mux21_24_d,
       mux21_25_d, mux21_26_d, mux21_27_d, mux21_28_d, mux21_29_d, mux21_30_d, mux21_31_d, mux21_32_d,
       mux21_33_d, mux21_34_d, mux21_35_d, mux21_36_d, mux21_37_d, mux21_38_d, mux21_39_d, mux21_40_d,
       not_1_out, not_2_out;

  and and_1 (and_1_out, in_1[7], not_1_out);
  not not_1 (not_1_out, aluc1);
  not not_2 (not_2_out, aluc0);
  MUX21 mux21_1 (.S1(1'b0), .S2(in_1[1]), .D(mux21_1_d), .C(not_2_out), .Ena(Ena));
  MUX21 mux21_2 (.S1(in_1[0]), .S2(in_1[2]), .D(mux21_2_d), .C(not_2_out), .Ena(Ena));
  MUX21 mux21_3 (.S1(in_1[1]), .S2(in_1[3]), .D(mux21_3_d), .C(not_2_out), .Ena(Ena));
  MUX21 mux21_4 (.S1(in_1[2]), .S2(in_1[4]), .D(mux21_4_d), .C(not_2_out), .Ena(Ena));
  MUX21 mux21_5 (.S1(in_1[3]), .S2(in_1[5]), .D(mux21_5_d), .C(not_2_out), .Ena(Ena));
  MUX21 mux21_6 (.S1(in_1[4]), .S2(in_1[6]), .D(mux21_6_d), .C(not_2_out), .Ena(Ena));
  MUX21 mux21_7 (.S1(in_1[5]), .S2(in_1[7]), .D(mux21_7_d), .C(not_2_out), .Ena(Ena));
  MUX21 mux21_8 (.S1(in_1[6]), .S2(and_1_out), .D(mux21_8_d), .C(not_2_out), .Ena(Ena));
  MUX21 mux21_9 (.S1(in_1[0]), .S2(mux21_1_d), .D(mux21_9_d), .C(in_5[0]), .Ena(Ena));
  MUX21 mux21_10 (.S1(in_1[1]), .S2(mux21_2_d), .D(mux21_10_d), .C(in_5[0]), .Ena(Ena));
  MUX21 mux21_11 (.S1(in_1[2]), .S2(mux21_3_d), .D(mux21_11_d), .C(in_5[0]), .Ena(Ena));
  MUX21 mux21_12 (.S1(in_1[3]), .S2(mux21_4_d), .D(mux21_12_d), .C(in_5[0]), .Ena(Ena));
  MUX21 mux21_13 (.S1(in_1[4]), .S2(mux21_5_d), .D(mux21_13_d), .C(in_5[0]), .Ena(Ena));
  MUX21 mux21_14 (.S1(in_1[5]), .S2(mux21_6_d), .D(mux21_14_d), .C(in_5[0]), .Ena(Ena));
  MUX21 mux21_15 (.S1(in_1[6]), .S2(mux21_7_d), .D(mux21_15_d), .C(in_5[0]), .Ena(Ena));
  MUX21 mux21_16 (.S1(in_1[7]), .S2(mux21_8_d), .D(mux21_16_d), .C(in_5[0]), .Ena(Ena));
  MUX21 mux21_17 (.S1(1'b0), .S2(mux21_11_d), .D(mux21_17_d), .C(not_2_out), .Ena(Ena));
  MUX21 mux21_18 (.S1(1'b0), .S2(mux21_12_d), .D(mux21_18_d), .C(not_2_out), .Ena(Ena));
  MUX21 mux21_19 (.S1(mux21_9_d), .S2(mux21_13_d), .D(mux21_19_d), .C(not_2_out), .Ena(Ena));
  MUX21 mux21_20 (.S1(mux21_10_d), .S2(mux21_14_d), .D(mux21_20_d), .C(not_2_out), .Ena(Ena));
  MUX21 mux21_21 (.S1(mux21_11_d), .S2(mux21_15_d), .D(mux21_21_d), .C(not_2_out), .Ena(Ena));
  MUX21 mux21_22 (.S1(mux21_12_d), .S2(mux21_16_d), .D(mux21_22_d), .C(not_2_out), .Ena(Ena));
  MUX21 mux21_23 (.S1(mux21_13_d), .S2(and_1_out), .D(mux21_23_d), .C(not_2_out), .Ena(Ena));
  MUX21 mux21_24 (.S1(mux21_14_d), .S2(and_1_out), .D(mux21_24_d), .C(not_2_out), .Ena(Ena));
  MUX21 mux21_25 (.S1(mux21_9_d), .S2(mux21_17_d), .D(mux21_25_d), .C(in_5[1]), .Ena(Ena));
  MUX21 mux21_26 (.S1(mux21_10_d), .S2(mux21_18_d), .D(mux21_26_d), .C(in_5[1]), .Ena(Ena));
  MUX21 mux21_27 (.S1(mux21_11_d), .S2(mux21_19_d), .D(mux21_27_d), .C(in_5[1]), .Ena(Ena));
  MUX21 mux21_28 (.S1(mux21_12_d), .S2(mux21_20_d), .D(mux21_28_d), .C(in_5[1]), .Ena(Ena));
  MUX21 mux21_29 (.S1(mux21_13_d), .S2(mux21_21_d), .D(mux21_29_d), .C(in_5[1]), .Ena(Ena));
  MUX21 mux21_30 (.S1(mux21_14_d), .S2(mux21_22_d), .D(mux21_30_d), .C(in_5[1]), .Ena(Ena));
  MUX21 mux21_31 (.S1(mux21_15_d), .S2(mux21_23_d), .D(mux21_31_d), .C(in_5[1]), .Ena(Ena));
  MUX21 mux21_32 (.S1(mux21_16_d), .S2(mux21_24_d), .D(mux21_32_d), .C(in_5[1]), .Ena(Ena));
  MUX21 mux21_33 (.S1(1'b0), .S2(mux21_29_d), .D(mux21_33_d), .C(not_2_out), .Ena(Ena));
  MUX21 mux21_34 (.S1(1'b0), .S2(mux21_30_d), .D(mux21_34_d), .C(not_2_out), .Ena(Ena));
  MUX21 mux21_35 (.S1(1'b0), .S2(mux21_31_d), .D(mux21_35_d), .C(not_2_out), .Ena(Ena));
  MUX21 mux21_36 (.S1(1'b0), .S2(mux21_32_d), .D(mux21_36_d), .C(not_2_out), .Ena(Ena));
  MUX21 mux21_37 (.S1(mux21_25_d), .S2(and_1_out), .D(mux21_37_d), .C(not_2_out), .Ena(Ena));
  MUX21 mux21_38 (.S1(mux21_26_d), .S2(and_1_out), .D(mux21_38_d), .C(not_2_out), .Ena(Ena));
  MUX21 mux21_39 (.S1(mux21_27_d), .S2(and_1_out), .D(mux21_39_d), .C(not_2_out), .Ena(Ena));
  MUX21 mux21_40 (.S1(mux21_28_d), .S2(and_1_out), .D(mux21_40_d), .C(not_2_out), .Ena(Ena));
  MUX21 mux21_41 (.S1(mux21_25_d), .S2(mux21_33_d), .D(out_6[0]), .C(in_5[2]), .Ena(Ena));
  MUX21 mux21_42 (.S1(mux21_26_d), .S2(mux21_34_d), .D(out_6[1]), .C(in_5[2]), .Ena(Ena));
  MUX21 mux21_43 (.S1(mux21_27_d), .S2(mux21_35_d), .D(out_6[2]), .C(in_5[2]), .Ena(Ena));
  MUX21 mux21_44 (.S1(mux21_28_d), .S2(mux21_36_d), .D(out_6[3]), .C(in_5[2]), .Ena(Ena));
  MUX21 mux21_45 (.S1(mux21_29_d), .S2(mux21_37_d), .D(out_6[4]), .C(in_5[2]), .Ena(Ena));
  MUX21 mux21_46 (.S1(mux21_30_d), .S2(mux21_38_d), .D(out_6[5]), .C(in_5[2]), .Ena(Ena));
  MUX21 mux21_47 (.S1(mux21_31_d), .S2(mux21_39_d), .D(out_6[6]), .C(in_5[2]), .Ena(Ena));
  MUX21 mux21_48 (.S1(mux21_32_d), .S2(mux21_40_d), .D(out_6[7]), .C(in_5[2]), .Ena(Ena));
endmodule
