// Logisim project 同步模8计数器.circ as structural Verilog: 1 circuit, main circuit main
module main (
  input  _1,
  input  rst,
  output Q2
);

  wire and_1_out, clock_out, FF0_q, FF1_q;

  Clock clock (.out(clock_out));
  J_K_Flip_Flop FF0 (.J(_1), .clk(clock_out), .K(_1), .Q(FF0_q), .en(_1), .reset(rst));  // open: Qn, preset
  J_K_Flip_Flop FF1 (.J(FF0_q), .clk(clock_out), .K(FF0_q), .Q(FF1_q), .en(_1), .reset(rst));  // open: Qn, preset
  and and_1 (and_1_out, FF0_q, FF1_q);
  J_K_Flip_Flop FF2 (.J(and_1_out), .clk(clock_out), .K(and_1_out), .Q(Q2), .en(_1), .reset(rst));  // open: Qn, preset
endmodule
