// Logisim project regfiles.circ as structural Verilog: 1 circuit, main circuit main
module main (
  input  rst,
  input  [3:0] wdata,
  input  we,
  input  [3:0] waddr,
  input  [3:0] raddr1,
  input  [3:0] raddr2,
  output [3:0] rdata1,
  output [3:0] rdata2
);

  wire clk_out, decoder_1_out0, decoder_1_out1, decoder_1_out2, decoder_1_out3, decoder_1_out4,
       decoder_1_out5, decoder_1_out6, decoder_1_out7, decoder_1_out8, decoder_1_out9, decoder_1_out10,
       decoder_1_out11, decoder_1_out12, decoder_1_out13, decoder_1_out14, decoder_1_out15;
  wire [3:0] register_1_q, register_2_q, register_3_q, register_4_q, register_5_q, register_6_q,
       register_7_q, register_8_q, register_9_q, register_10_q, register_11_q, register_12_q, register_13_q,
       register_14_q, register_15_q, register_16_q;

  Clock clk (.out(clk_out));
  Decoder #(.select(4), .disabled(0)) decoder_1 (
    .out0(decoder_1_out0), .out1(decoder_1_out1), .out2(decoder_1_out2), .out3(decoder_1_out3),
    .out4(decoder_1_out4), .out5(decoder_1_out5), .out6(decoder_1_out6), .out7(decoder_1_out7),
    .out8(decoder_1_out8), .out9(decoder_1_out9), .out10(decoder_1_out10), .out11(decoder_1_out11),
    .out12(decoder_1_out12), .out13(decoder_1_out13), .out14(decoder_1_out14), .out15(decoder_1_out15),
    .sel(waddr), .en(we));
  Register #(.width(4)) register_1 (.D(wdata), .en(decoder_1_out0), .Q(register_1_q), .clk(clk_out), .clr(rst));
  Register #(.width(4)) register_2 (.D(wdata), .en(decoder_1_out1), .Q(register_2_q), .clk(clk_out), .clr(rst));
  Register #(.width(4)) register_3 (.D(wdata), .en(decoder_1_out2), .Q(register_3_q), .clk(clk_out), .clr(rst));
  Register #(.width(4)) register_4 (.D(wdata), .en(decoder_1_out3), .Q(register_4_q), .clk(clk_out), .clr(rst));
  Register #(.width(4)) register_5 (.D(wdata), .en(decoder_1_out4), .Q(register_5_q), .clk(clk_out), .clr(rst));
  Register #(.width(4)) register_6 (.D(wdata), .en(decoder_1_out5), .Q(register_6_q), .clk(clk_out), .clr(rst));
  Register #(.width(4)) register_7 (.D(wdata), .en(decoder_1_out6), .Q(register_7_q), .clk(clk_out), .clr(rst));
  Register #(.width(4)) register_8 (.D(wdata), .en(decoder_1_out7), .Q(register_8_q), .clk(clk_out), .clr(rst));
  Register #(.width(4)) register_9 (.D(wdata), .en(decoder_1_out8), .Q(register_9_q), .clk(clk_out), .clr(rst));
  Register #(.width(4)) register_10 (.D(wdata), .en(decoder_1_out9), .Q(register_10_q), .clk(clk_out), .clr(rst));
  Register #(.width(4)) register_11 (.D(wdata), .en(decoder_1_out10), .Q(register_11_q), .clk(clk_out), .clr(rst));
  Register #(.width(4)) register_12 (.D(wdata), .en(decoder_1_out11), .Q(register_12_q), .clk(clk_out), .clr(rst));
  Register #(.width(4)) register_13 (.D(wdata), .en(decoder_1_out12), .Q(register_13_q), .clk(clk_out), .clr(rst));
  Register #(.width(4)) register_14 (.D(wdata), .en(decoder_1_out13), .Q(register_14_q), .clk(clk_out), .clr(rst));
  Register #(.width(4)) register_15 (.D(wdata), .en(decoder_1_out14), .Q(register_15_q), .clk(clk_out), .clr(rst));
  Register #(.width(4)) register_16 (.D(wdata), .en(decoder_1_out15), .Q(register_16_q), .clk(clk_out), .clr(rst));
  Multiplexer #(.select(4), .width(4), .enable("false")) multiplexer_1 (
    .in0(register_1_q), .in1(register_2_q), .in2(register_3_q), .in3(register_4_q), .in4(register_5_q),
    .in5(register_6_q), .in6(register_7_q), .in7(register_8_q), .in8(register_9_q), .in9(register_10_q),
    .in10(register_11_q), .in11(register_12_q), .in12(register_13_q), .in13(register_14_q),
    .in14(register_15_q), .in15(register_16_q), .out(rdata1), .sel(raddr1));
  Multiplexer #(.select(4), .width(4), .enable("false")) multiplexer_2 (
    .in0(register_1_q), .in1(register_2_q), .in2(register_3_q), .in3(register_4_q), .in4(register_5_q),
    .in5(register_6_q), .in6(register_7_q), .in7(register_8_q), .in8(register_9_q), .in9(register_10_q),
    .in10(register_11_q), .in11(register_12_q), .in12(register_13_q), .in13(register_14_q),
    .in14(register_15_q), .in15(register_16_q), .out(rdata2), .sel(raddr2));
endmodule
